# Fritzing sketch Circuito (saved by Fritzing 0.9.6b)
breadboards: 1

parts:
  Componente1 = RFID-RC522-v3
  Componente2 = Arduino Mega 2560 (Rev3)
  SG1 = Buzzer 12mm [part_number=COM-07950 package=buzzer-12mm-ns]
  R1 = Resistor [tolerance=±5% power=0.25 resistance=220 package=THT]
  R2 = Resistor [tolerance=±5% power=0.25 resistance=220 package=THT]
  LED1 = LED - 5mm [color="Red (633nm)" current=0.030 package="5 mm [THT]"]
  LED2 = LED - 5mm [color="Green (555nm)" current=0.030 package="5 mm [THT]"]

nets:
  N1: Componente1.SDA, Componente2.D9_PWM
  N2: Componente1.SCK, Componente2.D52
  N3: Componente1.MOSI, Componente2.D51
  N4: Componente1.MISO, Componente2.D50
  GND: Componente1.GND, Componente2.GND, SG1.2, R1.Pin_1, R2.Pin_1
  N5: Componente1.RST, Componente2.D8_PWM
  3.3V: Componente1.3.3V, Componente2.3V3
  N6: Componente2.D21/SCL, LED2.anode
  N7: Componente2.D20/SDA, LED1.anode
  N8: Componente2.D19/RX1, SG1.1
  N9: R1.Pin_0, LED1.cathode
  N10: R2.Pin_0, LED2.cathode

custom parts:
  RFID-RC522-v3: A simple China made RFID-RC522 Reader (6x4 cm); do check the pin labels, as this is a MFRC522 based clone.
  Buzzer 12mm: Buzzer 12mm Spark Fun Electronics SKU : Comp-Buzzer Through hole This is a small 12mm round speaker that operates around the audible 2kHz range. You can use these speakers to create simple music or user interfaces. This is not a true piezoelectric speaker but behaves similarly. Instead of a piezoelectric crystal that vibrates with an electric current, this tiny speaker uses an electromagnet to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
