# Fritzing sketch Cricuito (saved by Fritzing 0.9.6b)
breadboards: 1

parts:
  Componente1 = Arduino Mega 2560 (Rev3)
  Componente2 = Arduino Mega 2560 (Rev3)
  R1 = Resistor [tolerance=±5% power=0.25 resistance=220 package=THT]
  LED1 = LED - 5mm [color="Red (633nm)" current=0.030 package="5 mm [THT]"]
  R2 = Photocell (LDR) [package=THT]
  R3 = Resistor [tolerance=±5% power=0.25 resistance=220 package=THT]
  S1 = Pushbutton [package="[THT]"]

nets:
  N1: Componente1.D12_PWM, LED1.anode
  N2: Componente1.D11_PWM, Componente2.D10_PWM
  N3: Componente1.D10_PWM, Componente2.D11_PWM
  5V: Componente1.5V, Componente2.5V, R2.pin_0
  GND: Componente1.GND, Componente2.GND, R1.Pin_1, R3.Pin_0, S1.Pin_1, S1.Pin_2
  N4: Componente2.A0, R2.pin_1, R3.Pin_1
  N5: Componente2.D12_PWM, S1.Pin_3, S1.Pin_4
  N6: R1.Pin_0, LED1.cathode
