# Fritzing sketch Circuito (saved by Fritzing 0.9.6b)
breadboards: 2

parts:
  U1 = LuaNode32 / ESP32 [part_number=ESP32S-PIN30]
  R1 = Resistor [tolerance=±5% power=0.25 resistance=220 package=THT]
  LED1 = LED - 5mm [color="Red (633nm)" current=0.030 package="5 mm [THT]"]
  LED2 = LED - 5mm [color="Red (633nm)" current=0.030 package="5 mm [THT]"]
  R2 = Resistor [tolerance=±5% power=0.25 resistance=220 package=THT]

nets:
  N1: U1.GND, R1.Pin_0, R2.Pin_0
  N2: U1.D2, LED2.anode
  N3: U1.D22, LED1.anode
  N4: R1.Pin_1, LED1.cathode
  N5: LED2.cathode, R2.Pin_1

custom parts:
  LuaNode32 / ESP32: New Image for LuaNode32 DOIT ESP32 DEVKIT V1. Base parts from LuaNode32 / ESP32 ESP32 based LuaNode32 by G.Noorlander DOIT Esp32 DevKit v1 (30 pins long, 11 pins width) by Werner Rothschopf (modified by vanepp Dec 2018)
