# Fritzing sketch Circuito (saved by Fritzing 0.9.6b)
breadboards: 3

parts:
  Capacitive_Soil_Moisture_Sensor1 = DFRobot Capacitive Soil Moisture Sensor V1.0 [part_number=SEN0193]
  OLED1 = OLED 128x64 I2C Monochrome Display GND-VDD
  U1 = LuaNode32 / ESP32 [part_number=ESP32S-PIN30]
  DHT1 = DHT11 Humitidy and Temperature Sensor
  R1 = Photocell (LDR) [package=THT]
  R2 = Resistor [tolerance=±5% power=0.25 resistance=220 package=THT]

nets:
  N1: Capacitive_Soil_Moisture_Sensor1.A, U1.D35
  VDD: Capacitive_Soil_Moisture_Sensor1.VCC, OLED1.VDD, U1.3V3, DHT1.VDD, R1.pin_1
  GND: Capacitive_Soil_Moisture_Sensor1.GND, DHT1.GND, R2.Pin_1
  GND_2: OLED1.GND, U1.GND
  N2: OLED1.SCK, U1.D22
  N3: OLED1.SDA, U1.D21
  N4: U1.D34, R1.pin_0, R2.Pin_0
  N5: U1.D32, DHT1.DATA

custom parts:
  DFRobot Capacitive Soil Moisture Sensor V1.0: DFRobot Capacitive Soil Moisture Sensor V1.0 This product measures soil moisture levels by capacitive sensing, rather than resistive sensing like other types of moisture sensor. It is made of a corrosion resistant material giving it a long service life. Insert it into soil and impress your friends with the real-time soil moisture data! The product includes an on-board voltage regulator which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
  OLED 128x64 I2C Monochrome Display GND-VDD: OLED 128x64 I2C Monochrome Display. Note: there are two variants of this part, this one is the GND VDD SCK SDA variant. The other is VDD GND SCK SDA. Make sure you select the part that matches your module as using the incorrect part will probably destroy your module! In addition the mounting holes are marked on silkscreen but not by default drilled. If you want drilled mounting holes, copy a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
  LuaNode32 / ESP32: New Image for LuaNode32 DOIT ESP32 DEVKIT V1. Base parts from LuaNode32 / ESP32 ESP32 based LuaNode32 by G.Noorlander DOIT Esp32 DevKit v1 (30 pins long, 11 pins width) by Werner Rothschopf (modified by vanepp Dec 2018)
  DHT11 Humitidy and Temperature Sensor: DHT11 Humidity and Temperature Sensor
